// Logisim project circuit.circ as structural Verilog: 3 circuits, main circuit main
module main (
  input  in_1
);

  wire and_1_out, and_2_out, clock_1_out, cpu_1_j_e, cpu_1_j_m, not_1_out, xor_1_out;
  wire [3:0] cpu_1_f;
  wire [7:0] counter_1_q, cpu_1_j_a, cpu_1_o;
  wire [15:0] rom_1_data;

  Clock clock_1 (.out(clock_1_out));
  ROM #(.dataWidth(16)) rom_1 (.addr(counter_1_q), .data(rom_1_data));
  Counter counter_1 (
    .load(xor_1_out), .D(cpu_1_j_a), .count(1'b1), .Q(counter_1_q), .up(1'b1), .clk(clock_1_out), .clr(in_1));  // open: carry
  // Probe on cpu_1_o
  cpu cpu_1 (
    .I(rom_1_data), .CLK(clock_1_out), .O(cpu_1_o), .F(cpu_1_f), .J_a(cpu_1_j_a), .J_e(cpu_1_j_e),
    .J_m(cpu_1_j_m));
  // Probe on cpu_1_f
  and and_1 (and_1_out, cpu_1_j_e, not_1_out);
  not not_1 (not_1_out, cpu_1_j_m);
  xor xor_1 (xor_1_out, and_1_out, and_2_out);
  and and_2 (and_2_out, cpu_1_f[1], cpu_1_j_m);
endmodule

module alu (
  input  [7:0] A,
  input  [7:0] B,
  input  [2:0] OP,
  output [7:0] O,
  output [3:0] F
);

  wire xnor_1_out, xnor_2_out, xor_1_out;
  wire [7:0] adder_1_out, and_1_out, negator_1_out, not_1_out, or_1_out, shifter_1_out, shifter_2_out,
       subtractor_1_out;

  assign and_1_out = A & B;  // AND_Gate and_1, 8 bits wide
  assign or_1_out = A | B;  // OR_Gate or_1, 8 bits wide
  assign not_1_out = ~A;  // NOT_Gate not_1, 8 bits wide
  Negator negator_1 (.in(A), .out(negator_1_out));
  Adder adder_1 (.a(A), .b(B), .out(adder_1_out), .cout(F[2]));  // open: cin
  Subtractor subtractor_1 (.a(A), .b(B), .out(subtractor_1_out));  // open: bin, bout
  Shifter #(.shift("ar")) shifter_1 (.in(A), .\dist (B[2:0]), .out(shifter_1_out));
  Shifter shifter_2 (.in(A), .\dist (B[2:0]), .out(shifter_2_out));
  Multiplexer #(.select(3), .width(8)) multiplexer_1 (
    .in0(and_1_out), .in1(or_1_out), .in2(not_1_out), .in3(negator_1_out), .in4(adder_1_out),
    .in5(subtractor_1_out), .in6(shifter_1_out), .in7(shifter_2_out), .out({F[0], O[6:0]}), .sel(OP));
  nor nor_1 (F[1], O[0], O[1], O[2], O[3], O[4], O[5], O[6], F[0]);
  xnor xnor_1 (xnor_1_out, A[7], B[7]);
  xor xor_1 (xor_1_out, A[7], B[7]);
  xnor xnor_2 (xnor_2_out, F[2], xnor_1_out);
  xor xor_2 (F[3], xnor_2_out, xor_1_out);

  assign O[7] = F[0];
endmodule

module cpu (
  input  [15:0] I,
  input  CLK,
  output [7:0] O,
  output [3:0] F,
  output [7:0] J_a,
  output J_e,
  output J_m
);

  wire decoder_1_out0, decoder_1_out1, decoder_1_out2, decoder_1_out3, decoder_1_out4, decoder_1_out5,
       decoder_1_out6, decoder_1_out7, decoder_2_out1;
  wire [1:0] register_3_q_3;
  wire [2:0] register_3_q, register_3_q_2;
  wire [7:0] alu_1_o, demultiplexer_1_out0, demultiplexer_1_out1, demultiplexer_1_out2, demultiplexer_1_out3,
       demultiplexer_1_out4, demultiplexer_1_out5, demultiplexer_1_out6, demultiplexer_1_out7, ram_1_dout,
       register_1_q, register_2_q, register_4_q, register_5_q, register_6_q, register_7_q;

  Demultiplexer #(.select(3), .width(8)) demultiplexer_1 (
    .out0(demultiplexer_1_out0), .out1(demultiplexer_1_out1), .out2(demultiplexer_1_out2),
    .out3(demultiplexer_1_out3), .out4(demultiplexer_1_out4), .out5(demultiplexer_1_out5),
    .out6(demultiplexer_1_out6), .out7(demultiplexer_1_out7), .in(O), .sel(I[2:0]));
  Decoder #(.enable("false"), .select(3)) decoder_1 (
    .out0(decoder_1_out0), .out1(decoder_1_out1), .out2(decoder_1_out2), .out3(decoder_1_out3),
    .out4(decoder_1_out4), .out5(decoder_1_out5), .out6(decoder_1_out6), .out7(decoder_1_out7), .sel(I[2:0]));
  Decoder #(.enable("false"), .select(2)) decoder_2 (
    .out1(decoder_2_out1), .out2(J_e), .out3(J_m), .sel(I[7:6]));  // open: out0
  Register register_1 (.D(demultiplexer_1_out0), .en(decoder_1_out0), .Q(register_1_q), .clk(CLK));  // open: clr
  Register register_2 (.D(demultiplexer_1_out1), .en(decoder_1_out1), .Q(register_2_q), .clk(CLK));  // open: clr
  Register register_3 (
    .D(demultiplexer_1_out2), .en(decoder_1_out2), .Q({register_3_q_3, register_3_q_2, register_3_q}),
    .clk(CLK));  // open: clr
  Register register_4 (.D(demultiplexer_1_out3), .en(decoder_1_out3), .Q(register_4_q), .clk(CLK));  // open: clr
  Register register_5 (.D(demultiplexer_1_out4), .en(decoder_1_out4), .Q(register_5_q), .clk(CLK));  // open: clr
  Register register_6 (.D(demultiplexer_1_out5), .en(decoder_1_out5), .Q(register_6_q), .clk(CLK));  // open: clr
  Register register_7 (.D(demultiplexer_1_out6), .en(decoder_1_out6), .Q(register_7_q), .clk(CLK));  // open: clr
  Register register_8 (.D(demultiplexer_1_out7), .en(decoder_1_out7), .Q(J_a), .clk(CLK));  // open: clr
  RAM ram_1 (.addr(register_1_q), .we(decoder_2_out1), .oe(1'b1), .clk(CLK), .din(register_2_q), .dout(ram_1_dout));
  alu alu_1 (.A(register_1_q), .B(register_2_q), .OP(register_3_q), .O(alu_1_o), .F(F));
  Multiplexer #(.select(3), .width(8)) multiplexer_1 (
    .in0(alu_1_o), .in1({register_3_q_3, register_3_q_2, register_3_q}), .in2(register_4_q),
    .in3(register_5_q), .in4(register_6_q), .in5(ram_1_dout), .in6(register_7_q), .in7(I[15:8]), .out(O),
    .sel(I[5:3]));
endmodule
